// Logisim project Project.circ as structural Verilog: 5 circuits, main circuit Register File
module Register_File (
  input  [31:0] Write_data,
  input  [4:0] Read_Register_2,
  input  [4:0] Read_Register_1,
  input  [4:0] Write_Register,
  input  RegWrite,
  output [31:0] Read_Data_1,
  output [31:0] Read_Data_2
);

  wire and_1_out, and_2_out, and_3_out, and_4_out, and_5_out, and_6_out, and_7_out, and_8_out, and_9_out,
       and_10_out, and_11_out, and_12_out, and_13_out, and_14_out, and_15_out, and_16_out, and_17_out,
       and_18_out, and_19_out, and_20_out, and_21_out, and_22_out, and_23_out, and_24_out, and_25_out,
       and_26_out, and_27_out, and_28_out, and_29_out, and_30_out, and_31_out, and_32_out, clock_1_out,
       decoder_1_out0, decoder_1_out1, decoder_1_out2, decoder_1_out3, decoder_1_out4, decoder_1_out5,
       decoder_1_out6, decoder_1_out7, decoder_1_out8, decoder_1_out9, decoder_1_out10, decoder_1_out11,
       decoder_1_out12, decoder_1_out13, decoder_1_out14, decoder_1_out15, decoder_1_out16, decoder_1_out17,
       decoder_1_out18, decoder_1_out19, decoder_1_out20, decoder_1_out21, decoder_1_out22, decoder_1_out23,
       decoder_1_out24, decoder_1_out25, decoder_1_out26, decoder_1_out27, decoder_1_out28, decoder_1_out29,
       decoder_1_out30, decoder_1_out31;
  wire [31:0] register_1_q, register_2_q, register_3_q, register_4_q, register_5_q, register_6_q,
       register_7_q, register_8_q, register_9_q, register_10_q, register_11_q, register_12_q, register_13_q,
       register_14_q, register_15_q, register_16_q, register_17_q, register_18_q, register_19_q,
       register_20_q, register_21_q, register_22_q, register_23_q, register_24_q, register_25_q,
       register_26_q, register_27_q, register_28_q, register_29_q, register_30_q, register_31_q,
       register_32_q;

  Decoder #(.select(5), .enable("false")) decoder_1 (
    .out0(decoder_1_out0), .out1(decoder_1_out1), .out2(decoder_1_out2), .out3(decoder_1_out3),
    .out4(decoder_1_out4), .out5(decoder_1_out5), .out6(decoder_1_out6), .out7(decoder_1_out7),
    .out8(decoder_1_out8), .out9(decoder_1_out9), .out10(decoder_1_out10), .out11(decoder_1_out11),
    .out12(decoder_1_out12), .out13(decoder_1_out13), .out14(decoder_1_out14), .out15(decoder_1_out15),
    .out16(decoder_1_out16), .out17(decoder_1_out17), .out18(decoder_1_out18), .out19(decoder_1_out19),
    .out20(decoder_1_out20), .out21(decoder_1_out21), .out22(decoder_1_out22), .out23(decoder_1_out23),
    .out24(decoder_1_out24), .out25(decoder_1_out25), .out26(decoder_1_out26), .out27(decoder_1_out27),
    .out28(decoder_1_out28), .out29(decoder_1_out29), .out30(decoder_1_out30), .out31(decoder_1_out31),
    .sel(Write_Register));
  and and_1 (and_1_out, decoder_1_out0, RegWrite);
  and and_2 (and_2_out, decoder_1_out1, RegWrite);
  and and_3 (and_3_out, decoder_1_out2, RegWrite);
  and and_4 (and_4_out, decoder_1_out3, RegWrite);
  and and_5 (and_5_out, decoder_1_out4, RegWrite);
  and and_6 (and_6_out, decoder_1_out5, RegWrite);
  and and_7 (and_7_out, decoder_1_out6, RegWrite);
  and and_8 (and_8_out, decoder_1_out7, RegWrite);
  and and_9 (and_9_out, decoder_1_out8, RegWrite);
  and and_10 (and_10_out, decoder_1_out9, RegWrite);
  and and_11 (and_11_out, decoder_1_out10, RegWrite);
  and and_12 (and_12_out, decoder_1_out11, RegWrite);
  and and_13 (and_13_out, decoder_1_out12, RegWrite);
  and and_14 (and_14_out, decoder_1_out13, RegWrite);
  and and_15 (and_15_out, decoder_1_out14, RegWrite);
  and and_16 (and_16_out, decoder_1_out15, RegWrite);
  and and_17 (and_17_out, decoder_1_out16, RegWrite);
  and and_18 (and_18_out, decoder_1_out17, RegWrite);
  and and_19 (and_19_out, decoder_1_out18, RegWrite);
  and and_20 (and_20_out, decoder_1_out19, RegWrite);
  and and_21 (and_21_out, decoder_1_out20, RegWrite);
  and and_22 (and_22_out, decoder_1_out21, RegWrite);
  and and_23 (and_23_out, decoder_1_out22, RegWrite);
  and and_24 (and_24_out, decoder_1_out23, RegWrite);
  and and_25 (and_25_out, decoder_1_out24, RegWrite);
  and and_26 (and_26_out, decoder_1_out25, RegWrite);
  and and_27 (and_27_out, decoder_1_out26, RegWrite);
  and and_28 (and_28_out, decoder_1_out27, RegWrite);
  and and_29 (and_29_out, decoder_1_out28, RegWrite);
  and and_30 (and_30_out, decoder_1_out29, RegWrite);
  and and_31 (and_31_out, decoder_1_out30, RegWrite);
  and and_32 (and_32_out, decoder_1_out31, RegWrite);
  Clock clock_1 (.out(clock_1_out));
  Register #(.width(32)) register_1 (.D({32{1'b0}}), .en(and_1_out), .Q(register_1_q), .clk(clock_1_out));  // open: clr
  Register #(.width(32)) register_2 (.D(Write_data), .en(and_2_out), .Q(register_2_q), .clk(clock_1_out));  // open: clr
  Register #(.width(32)) register_3 (.D(Write_data), .en(and_3_out), .Q(register_3_q), .clk(clock_1_out));  // open: clr
  Register #(.width(32)) register_4 (.D(Write_data), .en(and_4_out), .Q(register_4_q), .clk(clock_1_out));  // open: clr
  Register #(.width(32)) register_5 (.D(Write_data), .en(and_5_out), .Q(register_5_q), .clk(clock_1_out));  // open: clr
  Register #(.width(32)) register_6 (.D(Write_data), .en(and_6_out), .Q(register_6_q), .clk(clock_1_out));  // open: clr
  Register #(.width(32)) register_7 (.D(Write_data), .en(and_7_out), .Q(register_7_q), .clk(clock_1_out));  // open: clr
  Register #(.width(32), .trigger("high")) register_8 (
    .D(Write_data), .en(and_8_out), .Q(register_8_q), .clk(clock_1_out));  // open: clr
  Register #(.width(32)) register_9 (.D(Write_data), .en(and_9_out), .Q(register_9_q), .clk(clock_1_out));  // open: clr
  Register #(.width(32)) register_10 (
    .D(Write_data), .en(and_10_out), .Q(register_10_q), .clk(clock_1_out));  // open: clr
  Register #(.width(32)) register_11 (
    .D(Write_data), .en(and_11_out), .Q(register_11_q), .clk(clock_1_out));  // open: clr
  Register #(.width(32)) register_12 (
    .D(Write_data), .en(and_12_out), .Q(register_12_q), .clk(clock_1_out));  // open: clr
  Register #(.width(32)) register_13 (
    .D(Write_data), .en(and_13_out), .Q(register_13_q), .clk(clock_1_out));  // open: clr
  Register #(.width(32)) register_14 (
    .D(Write_data), .en(and_14_out), .Q(register_14_q), .clk(clock_1_out));  // open: clr
  Register #(.width(32)) register_15 (
    .D(Write_data), .en(and_15_out), .Q(register_15_q), .clk(clock_1_out));  // open: clr
  Register #(.width(32)) register_16 (
    .D(Write_data), .en(and_16_out), .Q(register_16_q), .clk(clock_1_out));  // open: clr
  Register #(.width(32)) register_17 (
    .D(Write_data), .en(and_17_out), .Q(register_17_q), .clk(clock_1_out));  // open: clr
  Register #(.width(32)) register_18 (
    .D(Write_data), .en(and_18_out), .Q(register_18_q), .clk(clock_1_out));  // open: clr
  Register #(.width(32)) register_19 (
    .D(Write_data), .en(and_19_out), .Q(register_19_q), .clk(clock_1_out));  // open: clr
  Register #(.width(32)) register_20 (
    .D(Write_data), .en(and_20_out), .Q(register_20_q), .clk(clock_1_out));  // open: clr
  Register #(.width(32)) register_21 (
    .D(Write_data), .en(and_21_out), .Q(register_21_q), .clk(clock_1_out));  // open: clr
  Register #(.width(32)) register_22 (
    .D(Write_data), .en(and_22_out), .Q(register_22_q), .clk(clock_1_out));  // open: clr
  Register #(.width(32)) register_23 (
    .D(Write_data), .en(and_23_out), .Q(register_23_q), .clk(clock_1_out));  // open: clr
  Register #(.width(32)) register_24 (
    .D(Write_data), .en(and_24_out), .Q(register_24_q), .clk(clock_1_out));  // open: clr
  Register #(.width(32)) register_25 (
    .D(Write_data), .en(and_25_out), .Q(register_25_q), .clk(clock_1_out));  // open: clr
  Register #(.width(32)) register_26 (
    .D(Write_data), .en(and_26_out), .Q(register_26_q), .clk(clock_1_out));  // open: clr
  Register #(.width(32)) register_27 (
    .D(Write_data), .en(and_27_out), .Q(register_27_q), .clk(clock_1_out));  // open: clr
  Register #(.width(32)) register_28 (
    .D(Write_data), .en(and_28_out), .Q(register_28_q), .clk(clock_1_out));  // open: clr
  Register #(.width(32)) register_29 (
    .D(Write_data), .en(and_29_out), .Q(register_29_q), .clk(clock_1_out));  // open: clr
  Register #(.width(32)) register_30 (
    .D(Write_data), .en(and_30_out), .Q(register_30_q), .clk(clock_1_out));  // open: clr
  Register #(.width(32)) register_31 (
    .D(Write_data), .en(and_31_out), .Q(register_31_q), .clk(clock_1_out));  // open: clr
  Register #(.width(32)) register_32 (
    .D(Write_data), .en(and_32_out), .Q(register_32_q), .clk(clock_1_out));  // open: clr
  Multiplexer #(.select(5), .width(32), .enable("false")) multiplexer_1 (
    .in0(register_1_q), .in1(register_2_q), .in2(register_3_q), .in3(register_4_q), .in4(register_5_q),
    .in5(register_6_q), .in6(register_7_q), .in7(register_8_q), .in8(register_9_q), .in9(register_10_q),
    .in10(register_11_q), .in11(register_12_q), .in12(register_13_q), .in13(register_14_q),
    .in14(register_15_q), .in15(register_16_q), .in16(register_17_q), .in17(register_18_q),
    .in18(register_19_q), .in19(register_20_q), .in20(register_21_q), .in21(register_22_q),
    .in22(register_23_q), .in23(register_24_q), .in24(register_25_q), .in25(register_26_q),
    .in26(register_27_q), .in27(register_28_q), .in28(register_29_q), .in29(register_30_q),
    .in30(register_31_q), .in31(register_32_q), .out(Read_Data_1), .sel(Read_Register_1));
  Multiplexer #(.select(5), .width(32), .enable("false")) multiplexer_2 (
    .in0(register_1_q), .in1(register_2_q), .in2(register_3_q), .in3(register_4_q), .in4(register_5_q),
    .in5(register_6_q), .in6(register_7_q), .in7(register_8_q), .in8(register_9_q), .in9(register_10_q),
    .in10(register_11_q), .in11(register_12_q), .in12(register_13_q), .in13(register_14_q),
    .in14(register_15_q), .in15(register_16_q), .in16(register_17_q), .in17(register_18_q),
    .in18(register_19_q), .in19(register_20_q), .in20(register_21_q), .in21(register_22_q),
    .in22(register_23_q), .in23(register_24_q), .in24(register_25_q), .in25(register_26_q),
    .in26(register_27_q), .in27(register_28_q), .in28(register_29_q), .in29(register_30_q),
    .in30(register_31_q), .in31(register_32_q), .out(Read_Data_2), .sel(Read_Register_2));

  // Notes on the sheet:
  //   Clock
endmodule

module ALU_32_bit (
  input  [31:0] A,
  input  [31:0] B,
  input  Carry_In,
  input  Binvert,
  input  Ainvert,
  input  [1:0] Operation,
  input  [2:0] ResCtrl,
  input  [1:0] ShftCtrl,
  output ZeroFlag,
  output [31:0] AluResult,
  output Overflow,
  output Carry_Out
);

  wire alu_1_bit_1_carry_out, alu_1_bit_2_carry_out, alu_1_bit_3_carry_out, alu_1_bit_4_carry_out,
       alu_1_bit_5_carry_out, alu_1_bit_6_carry_out, alu_1_bit_7_carry_out, alu_1_bit_8_carry_out,
       alu_1_bit_9_carry_out, alu_1_bit_10_carry_out, alu_1_bit_11_carry_out, alu_1_bit_12_carry_out,
       alu_1_bit_13_carry_out, alu_1_bit_14_carry_out, alu_1_bit_15_carry_out, alu_1_bit_16_carry_out,
       alu_1_bit_17_carry_out, alu_1_bit_18_carry_out, alu_1_bit_19_carry_out, alu_1_bit_20_carry_out,
       alu_1_bit_21_carry_out, alu_1_bit_22_carry_out, alu_1_bit_23_carry_out, alu_1_bit_24_carry_out,
       alu_1_bit_25_carry_out, alu_1_bit_26_carry_out, alu_1_bit_27_carry_out, alu_1_bit_28_carry_out,
       alu_1_bit_29_carry_out, alu_1_bit_30_carry_out, alu_1_bit_31_carry_out, and_1_out, and_2_out,
       and_3_out, comparator_1_eq, comparator_1_gt, comparator_1_lt, comparator_2_eq, comparator_2_gt,
       comparator_2_lt, comparator_3_eq, comparator_3_gt, comparator_3_lt, not_2_out, not_3_out, not_4_out,
       not_5_out, not_6_out, not_7_out, or_1_out, R0, R1, R2, R3, R4, R5, R6, R7, R8, R9, R10, R11, R12, R13,
       R14, R15, R16, R17, R18, R19, R20, R21, R22, R23, R24, R25, R26, R27, R28, R29, R30, R31;
  wire [30:0] multiplier_1_out;
  wire [31:0] bit_extender_1_out, bit_extender_2_out, bit_extender_3_out, bit_extender_4_out,
       multiplexer_1_out, shifter_1_out, shifter_2_out, shifter_3_out, shifter_4_out;
  wire [31:31] xor_2_out;

  ALU_1_bit alu_1_bit_1 (
    .A(A[0]), .B(B[0]), .Carry_In(Carry_In), .Result(R0), .Carry_Out(alu_1_bit_1_carry_out),
    .Ainvert(Ainvert), .Binvert(Binvert), .Operation(Operation));
  ALU_1_bit alu_1_bit_2 (
    .A(A[1]), .B(B[1]), .Carry_In(alu_1_bit_1_carry_out), .Result(R1), .Carry_Out(alu_1_bit_2_carry_out),
    .Ainvert(Ainvert), .Binvert(Binvert), .Operation(Operation));
  ALU_1_bit alu_1_bit_3 (
    .A(A[2]), .B(B[2]), .Carry_In(alu_1_bit_2_carry_out), .Result(R2), .Carry_Out(alu_1_bit_3_carry_out),
    .Ainvert(Ainvert), .Binvert(Binvert), .Operation(Operation));
  ALU_1_bit alu_1_bit_4 (
    .A(A[3]), .B(B[3]), .Carry_In(alu_1_bit_3_carry_out), .Result(R3), .Carry_Out(alu_1_bit_4_carry_out),
    .Ainvert(Ainvert), .Binvert(Binvert), .Operation(Operation));
  ALU_1_bit alu_1_bit_5 (
    .A(A[4]), .B(B[4]), .Carry_In(alu_1_bit_4_carry_out), .Result(R4), .Carry_Out(alu_1_bit_5_carry_out),
    .Ainvert(Ainvert), .Binvert(Binvert), .Operation(Operation));
  ALU_1_bit alu_1_bit_6 (
    .A(A[5]), .B(B[5]), .Carry_In(alu_1_bit_5_carry_out), .Result(R5), .Carry_Out(alu_1_bit_6_carry_out),
    .Ainvert(Ainvert), .Binvert(Binvert), .Operation(Operation));
  ALU_1_bit alu_1_bit_7 (
    .A(A[6]), .B(B[6]), .Carry_In(alu_1_bit_6_carry_out), .Result(R6), .Carry_Out(alu_1_bit_7_carry_out),
    .Ainvert(Ainvert), .Binvert(Binvert), .Operation(Operation));
  ALU_1_bit alu_1_bit_8 (
    .A(A[7]), .B(B[7]), .Carry_In(alu_1_bit_7_carry_out), .Result(R7), .Carry_Out(alu_1_bit_8_carry_out),
    .Ainvert(Ainvert), .Binvert(Binvert), .Operation(Operation));
  ALU_1_bit alu_1_bit_9 (
    .A(A[8]), .B(B[8]), .Carry_In(alu_1_bit_8_carry_out), .Result(R8), .Carry_Out(alu_1_bit_9_carry_out),
    .Ainvert(Ainvert), .Binvert(Binvert), .Operation(Operation));
  ALU_1_bit alu_1_bit_10 (
    .A(A[9]), .B(B[9]), .Carry_In(alu_1_bit_9_carry_out), .Result(R9), .Carry_Out(alu_1_bit_10_carry_out),
    .Ainvert(Ainvert), .Binvert(Binvert), .Operation(Operation));
  ALU_1_bit alu_1_bit_11 (
    .A(A[10]), .B(B[10]), .Carry_In(alu_1_bit_10_carry_out), .Result(R10),
    .Carry_Out(alu_1_bit_11_carry_out), .Ainvert(Ainvert), .Binvert(Binvert), .Operation(Operation));
  ALU_1_bit alu_1_bit_12 (
    .A(A[11]), .B(B[11]), .Carry_In(alu_1_bit_11_carry_out), .Result(R11),
    .Carry_Out(alu_1_bit_12_carry_out), .Ainvert(Ainvert), .Binvert(Binvert), .Operation(Operation));
  ALU_1_bit alu_1_bit_13 (
    .A(A[12]), .B(B[12]), .Carry_In(alu_1_bit_12_carry_out), .Result(R12),
    .Carry_Out(alu_1_bit_13_carry_out), .Ainvert(Ainvert), .Binvert(Binvert), .Operation(Operation));
  ALU_1_bit alu_1_bit_14 (
    .A(A[13]), .B(B[13]), .Carry_In(alu_1_bit_13_carry_out), .Result(R13),
    .Carry_Out(alu_1_bit_14_carry_out), .Ainvert(Ainvert), .Binvert(Binvert), .Operation(Operation));
  ALU_1_bit alu_1_bit_15 (
    .A(A[14]), .B(B[14]), .Carry_In(alu_1_bit_14_carry_out), .Result(R14),
    .Carry_Out(alu_1_bit_15_carry_out), .Ainvert(Ainvert), .Binvert(Binvert), .Operation(Operation));
  ALU_1_bit alu_1_bit_16 (
    .A(A[15]), .B(B[15]), .Carry_In(alu_1_bit_15_carry_out), .Result(R15),
    .Carry_Out(alu_1_bit_16_carry_out), .Ainvert(Ainvert), .Binvert(Binvert), .Operation(Operation));
  ALU_1_bit alu_1_bit_17 (
    .A(A[16]), .B(B[16]), .Carry_In(alu_1_bit_16_carry_out), .Result(R16),
    .Carry_Out(alu_1_bit_17_carry_out), .Ainvert(Ainvert), .Binvert(Binvert), .Operation(Operation));
  ALU_1_bit alu_1_bit_18 (
    .A(A[17]), .B(B[17]), .Carry_In(alu_1_bit_17_carry_out), .Result(R17),
    .Carry_Out(alu_1_bit_18_carry_out), .Ainvert(Ainvert), .Binvert(Binvert), .Operation(Operation));
  ALU_1_bit alu_1_bit_19 (
    .A(A[18]), .B(B[18]), .Carry_In(alu_1_bit_18_carry_out), .Result(R18),
    .Carry_Out(alu_1_bit_19_carry_out), .Ainvert(Ainvert), .Binvert(Binvert), .Operation(Operation));
  ALU_1_bit alu_1_bit_20 (
    .A(A[19]), .B(B[19]), .Carry_In(alu_1_bit_19_carry_out), .Result(R19),
    .Carry_Out(alu_1_bit_20_carry_out), .Ainvert(Ainvert), .Binvert(Binvert), .Operation(Operation));
  ALU_1_bit alu_1_bit_21 (
    .A(A[20]), .B(B[20]), .Carry_In(alu_1_bit_20_carry_out), .Result(R20),
    .Carry_Out(alu_1_bit_21_carry_out), .Ainvert(Ainvert), .Binvert(Binvert), .Operation(Operation));
  ALU_1_bit alu_1_bit_22 (
    .A(A[21]), .B(B[21]), .Carry_In(alu_1_bit_21_carry_out), .Result(R21),
    .Carry_Out(alu_1_bit_22_carry_out), .Ainvert(Ainvert), .Binvert(Binvert), .Operation(Operation));
  ALU_1_bit alu_1_bit_23 (
    .A(A[22]), .B(B[22]), .Carry_In(alu_1_bit_22_carry_out), .Result(R22),
    .Carry_Out(alu_1_bit_23_carry_out), .Ainvert(Ainvert), .Binvert(Binvert), .Operation(Operation));
  ALU_1_bit alu_1_bit_24 (
    .A(A[23]), .B(B[23]), .Carry_In(alu_1_bit_23_carry_out), .Result(R23),
    .Carry_Out(alu_1_bit_24_carry_out), .Ainvert(Ainvert), .Binvert(Binvert), .Operation(Operation));
  ALU_1_bit alu_1_bit_25 (
    .A(A[24]), .B(B[24]), .Carry_In(alu_1_bit_24_carry_out), .Result(R24),
    .Carry_Out(alu_1_bit_25_carry_out), .Ainvert(Ainvert), .Binvert(Binvert), .Operation(Operation));
  ALU_1_bit alu_1_bit_26 (
    .A(A[25]), .B(B[25]), .Carry_In(alu_1_bit_25_carry_out), .Result(R25),
    .Carry_Out(alu_1_bit_26_carry_out), .Ainvert(Ainvert), .Binvert(Binvert), .Operation(Operation));
  ALU_1_bit alu_1_bit_27 (
    .A(A[26]), .B(B[26]), .Carry_In(alu_1_bit_26_carry_out), .Result(R26),
    .Carry_Out(alu_1_bit_27_carry_out), .Ainvert(Ainvert), .Binvert(Binvert), .Operation(Operation));
  ALU_1_bit alu_1_bit_28 (
    .A(A[27]), .B(B[27]), .Carry_In(alu_1_bit_27_carry_out), .Result(R27),
    .Carry_Out(alu_1_bit_28_carry_out), .Ainvert(Ainvert), .Binvert(Binvert), .Operation(Operation));
  ALU_1_bit alu_1_bit_29 (
    .A(A[28]), .B(B[28]), .Carry_In(alu_1_bit_28_carry_out), .Result(R28),
    .Carry_Out(alu_1_bit_29_carry_out), .Ainvert(Ainvert), .Binvert(Binvert), .Operation(Operation));
  ALU_1_bit alu_1_bit_30 (
    .A(A[29]), .B(B[29]), .Carry_In(alu_1_bit_29_carry_out), .Result(R29),
    .Carry_Out(alu_1_bit_30_carry_out), .Ainvert(Ainvert), .Binvert(Binvert), .Operation(Operation));
  ALU_1_bit alu_1_bit_31 (
    .A(A[30]), .B(B[30]), .Carry_In(alu_1_bit_30_carry_out), .Result(R30),
    .Carry_Out(alu_1_bit_31_carry_out), .Ainvert(Ainvert), .Binvert(Binvert), .Operation(Operation));
  ALU_1_bit alu_1_bit_32 (
    .A(A[31]), .B(B[31]), .Carry_In(alu_1_bit_31_carry_out), .Result(R31), .Carry_Out(Carry_Out),
    .Ainvert(Ainvert), .Binvert(Binvert), .Operation(Operation));
  xor xor_1 (Overflow, alu_1_bit_31_carry_out, Carry_Out);
  not not_1 (ZeroFlag, or_1_out);
  or or_1 (or_1_out, R0, R1, R2, R3, R4, R5, R6, R7, R8, R9, R10, R11, R12, R13, R14, R15, R16, R17, R18, R19, R20, R21, R22, R23, R24, R25, R26, R27, R28, R29, R30, R31);
  Shifter #(.width(32)) shifter_1 (.in(A), .\dist (B[4:0]), .out(shifter_1_out));
  Shifter #(.width(32), .shift("lr")) shifter_2 (.in(A), .\dist (B[4:0]), .out(shifter_2_out));
  Shifter #(.width(32), .shift("ar")) shifter_3 (.in(A), .\dist (B[4:0]), .out(shifter_3_out));
  Shifter #(.width(32), .shift("rr")) shifter_4 (.in(A), .\dist (B[4:0]), .out(shifter_4_out));
  not not_2 (not_2_out, comparator_1_gt);
  Comparator #(.width(32)) comparator_1 (
    .a(A), .b(B), .gt(comparator_1_gt), .eq(comparator_1_eq), .lt(comparator_1_lt));
  not not_3 (not_3_out, comparator_1_eq);
  not not_4 (not_4_out, comparator_2_gt);
  Comparator #(.width(32), .mode("unsigned")) comparator_2 (
    .a(A), .b(B), .gt(comparator_2_gt), .eq(comparator_2_eq), .lt(comparator_2_lt));
  not not_5 (not_5_out, comparator_2_eq);
  not not_6 (not_6_out, comparator_3_gt);
  Comparator #(.width(32), .mode("unsigned")) comparator_3 (
    .a(A), .b(B), .gt(comparator_3_gt), .eq(comparator_3_eq), .lt(comparator_3_lt));
  not not_7 (not_7_out, comparator_3_lt);
  assign bit_extender_1_out = {{31{1'b0}}, R31};  // Bit_Extender bit_extender_1
  Multiplier #(.width(31)) multiplier_1 (.a(A[30:0]), .b(B[30:0]), .out(multiplier_1_out));  // open: cin, cout
  xor xor_2 (xor_2_out[31], A[31], B[31]);
  Multiplexer #(.select(2), .width(32), .enable("false")) multiplexer_1 (
    .in0(shifter_1_out), .in1(shifter_2_out), .in2(shifter_3_out), .in3(shifter_4_out),
    .out(multiplexer_1_out), .sel(ShftCtrl));
  and and_1 (and_1_out, not_2_out, not_3_out, comparator_1_lt);
  and and_2 (and_2_out, not_4_out, not_5_out, comparator_2_lt);
  and and_3 (and_3_out, not_6_out, comparator_3_eq, not_7_out);
  assign bit_extender_2_out = {{31{1'b0}}, and_1_out};  // Bit_Extender bit_extender_2
  assign bit_extender_3_out = {{31{1'b0}}, and_2_out};  // Bit_Extender bit_extender_3
  assign bit_extender_4_out = {{31{1'b0}}, and_3_out};  // Bit_Extender bit_extender_4
  Multiplexer #(.select(3), .width(32), .enable("false")) multiplexer_2 (
    .in0({R31, R30, R29, R28, R27, R26, R25, R24, R23, R22, R21, R20, R19, R18, R17, R16, R15, R14, R13, R12, R11, R10, R9, R8, R7, R6, R5, R4, R3, R2, R1, R0}),
    .in1(multiplexer_1_out), .in2(bit_extender_2_out), .in3(bit_extender_3_out), .in4(bit_extender_4_out),
    .in5(bit_extender_1_out), .in6({xor_2_out[31], multiplier_1_out}), .out(AluResult), .sel(ResCtrl));  // open: in7

  // Other names for the same wires on the sheet: b_t[4:0] = B[4:0]

  // Notes on the sheet:
  //   SLL
  //   SRL
  //   SRA
  //   ROR
  //   BEQ / BNE
  //   BEQ / BNE
  //   SEQ
  //   SLT
  //   MUL
  //   Signed
  //   Unsigned
endmodule

module Next_PC (
  input  [4:0] ImmL_5,
  input  [10:0] ImmU_11,
  input  [15:0] Imm_16,
  input  [1:0] PCsrc,
  input  [31:0] Rs1_Test_Input_554d0cdc
);

  wire clock_1_out;
  wire [19:0] adder_1_out, adder_2_out, bit_extender_1_out, multiplexer_1_out, PC_q;
  wire [31:0] adder_3_out, bit_extender_2_out, Rs1_q;

  Clock clock_1 (.out(clock_1_out));
  Register #(.width(20)) PC (.D(multiplexer_1_out), .Q(PC_q), .clk(clock_1_out));  // open: en, clr
  Adder #(.width(20)) adder_1 (.a(PC_q), .b(20'h1), .out(adder_1_out));  // open: cin, cout
  // Probe on adder_1_out
  assign bit_extender_1_out = {{4{1'b0}}, {ImmU_11, ImmL_5}};  // Bit_Extender bit_extender_1
  assign bit_extender_2_out = {{16{1'b0}}, Imm_16};  // Bit_Extender bit_extender_2
  Register #(.width(32)) Rs1 (.D(Rs1_Test_Input_554d0cdc), .Q(Rs1_q), .clk(clock_1_out));  // open: en, clr
  Adder #(.width(20)) adder_2 (.a(adder_1_out), .b(bit_extender_1_out), .out(adder_2_out), .cin(1'b0));  // open: cout
  Adder #(.width(32)) adder_3 (.a(bit_extender_2_out), .b(Rs1_q), .out(adder_3_out), .cin(1'b0));  // open: cout
  // Probe on adder_2_out
  // Probe on adder_3_out[19:0]
  Multiplexer #(.select(2), .width(20), .enable("false")) multiplexer_1 (
    .in0(adder_1_out), .in1(adder_2_out), .in2(adder_3_out[19:0]), .out(multiplexer_1_out), .sel(PCsrc));  // open: in3

  // Notes on the sheet:
  //   PC + 1
  //   PC + 1
endmodule

module ALU_1_bit (
  input  A,
  input  Ainvert,
  input  B,
  input  Binvert,
  input  [1:0] Operation,
  input  Carry_In,
  output Result,
  output Carry_Out
);

  wire adder_1_out, and_1_out, multiplexer_1_out, multiplexer_2_out, not_1_out, not_2_out, or_1_out,
       xor_1_out;

  Multiplexer #(.enable("false")) multiplexer_1 (.in0(A), .in1(not_1_out), .out(multiplexer_1_out), .sel(Ainvert));
  not not_1 (not_1_out, A);
  Multiplexer #(.enable("false")) multiplexer_2 (.in0(B), .in1(not_2_out), .out(multiplexer_2_out), .sel(Binvert));
  not not_2 (not_2_out, B);
  and and_1 (and_1_out, multiplexer_1_out, multiplexer_2_out);
  or or_1 (or_1_out, multiplexer_1_out, multiplexer_2_out);
  xor xor_1 (xor_1_out, multiplexer_1_out, multiplexer_2_out);
  Adder #(.width(1)) adder_1 (
    .a(multiplexer_1_out), .b(multiplexer_2_out), .out(adder_1_out), .cin(Carry_In), .cout(Carry_Out));
  Multiplexer #(.select(2), .enable("false")) multiplexer_3 (
    .in0(and_1_out), .in1(or_1_out), .in2(xor_1_out), .in3(adder_1_out), .out(Result), .sel(Operation));
endmodule

module Main_Control_Unit (
  input  op5,
  input  op4,
  input  op3,
  input  op2,
  input  op1,
  input  op0,
  output RegDst,
  output RegWrite,
  output ALUsrc,
  output MemRead,
  output MemWrite,
  output MemToReg,
  output Branch,
  output JumpAL,
  output ExtOp,
  output ALUctrl1,
  output ALUctrl0
);

  wire and_1_out, and_2_out, and_4_out, and_5_out, and_6_out, and_7_out, and_8_out, and_9_out, and_10_out,
       and_11_out, and_12_out, and_13_out, and_16_out, and_17_out, and_18_out, and_19_out, and_20_out,
       and_21_out, and_22_out, and_23_out, and_24_out, and_25_out, and_26_out, and_27_out, not_1_out,
       not_2_out, not_3_out, not_4_out, not_5_out, not_6_out, not_7_out, not_8_out, not_9_out, not_10_out,
       not_11_out, not_12_out, not_13_out, not_14_out, not_15_out, not_16_out, not_17_out, not_18_out,
       not_19_out, not_20_out, not_21_out, not_22_out, not_23_out, not_24_out, not_25_out, not_26_out,
       not_27_out, not_28_out, not_29_out, not_30_out, not_31_out, not_32_out, not_33_out, not_34_out,
       not_35_out, not_36_out, not_37_out, not_38_out;

  not not_1 (not_1_out, op4);
  not not_2 (not_2_out, op3);
  not not_3 (not_3_out, op2);
  not not_4 (not_4_out, op1);
  not not_5 (not_5_out, op0);
  not not_6 (not_6_out, op2);
  not not_7 (not_7_out, op1);
  not not_8 (not_8_out, op0);
  not not_9 (not_9_out, op4);
  not not_10 (not_10_out, op3);
  not not_11 (not_11_out, op4);
  not not_12 (not_12_out, op3);
  not not_13 (not_13_out, op4);
  not not_14 (not_14_out, op3);
  not not_15 (not_15_out, op2);
  not not_16 (not_16_out, op1);
  not not_17 (not_17_out, op0);
  not not_18 (not_18_out, op2);
  not not_19 (not_19_out, op1);
  not not_20 (not_20_out, op2);
  not not_21 (not_21_out, op1);
  not not_22 (not_22_out, op0);
  not not_23 (not_23_out, op2);
  not not_24 (not_24_out, op1);
  not not_25 (not_25_out, op0);
  and and_1 (and_1_out, op4, op1);
  and and_2 (and_2_out, op4, op2);
  and and_3 (JumpAL, op3, op2, op1, op0);
  not not_26 (not_26_out, op2);
  not not_27 (not_27_out, op1);
  not not_28 (not_28_out, op0);
  not not_29 (not_29_out, op1);
  not not_30 (not_30_out, op0);
  not not_31 (not_31_out, op4);
  not not_32 (not_32_out, op3);
  not not_33 (not_33_out, op2);
  not not_34 (not_34_out, op1);
  not not_35 (not_35_out, op0);
  not not_36 (not_36_out, op0);
  not not_37 (not_37_out, op0);
  and and_4 (and_4_out, not_1_out, not_2_out, not_3_out, not_4_out, not_5_out);
  and and_5 (and_5_out, op3, op2, op1, op0);
  not not_38 (not_38_out, op4);
  and and_6 (and_6_out, not_6_out, not_7_out, not_8_out);
  and and_7 (and_7_out, not_9_out, not_10_out, op0);
  and and_8 (and_8_out, not_11_out, not_12_out, op1);
  and and_9 (and_9_out, not_13_out, not_14_out, op2);
  and and_10 (and_10_out, op3, not_15_out);
  and and_11 (and_11_out, op3, not_16_out);
  and and_12 (and_12_out, op3, not_17_out);
  and and_13 (and_13_out, op4, not_18_out, not_19_out);
  and and_14 (MemRead, op4, not_20_out, not_21_out, not_22_out);
  and and_15 (MemWrite, op4, not_23_out, not_24_out, op0);
  and and_16 (and_16_out, op4, not_25_out);
  and and_17 (and_17_out, op4, op1);
  or or_1 (Branch, and_1_out, and_2_out);
  and and_18 (and_18_out, not_26_out, not_27_out, not_28_out);
  and and_19 (and_19_out, op2, not_29_out, op0);
  and and_20 (and_20_out, op2, op1, not_30_out);
  and and_21 (and_21_out, op3, op2, op1);
  and and_22 (and_22_out, not_31_out, not_32_out, not_33_out, not_34_out, not_35_out);
  and and_23 (and_23_out, op3, op2, op1, not_36_out);
  and and_24 (and_24_out, op3, op2, op1, not_37_out);
  and and_25 (and_25_out, op4, op0);
  and and_26 (and_26_out, op4, op1);
  and and_27 (and_27_out, op4, op2);
  or or_2 (RegDst, and_4_out, and_5_out);
  or or_3 (RegWrite, not_38_out, and_6_out);
  or or_4 (ALUsrc, and_7_out, and_8_out, and_9_out, and_10_out, and_11_out, and_12_out, and_13_out);
  or or_5 (MemToReg, and_16_out, and_17_out);
  or or_6 (ExtOp, and_18_out, and_19_out, and_20_out, and_21_out, op4);
  or or_7 (ALUctrl1, and_22_out, and_23_out);
  or or_8 (ALUctrl0, and_24_out, and_25_out, and_26_out, and_27_out);
endmodule
