// Logisim project TestOne.circ as structural Verilog: 1 circuit, main circuit main
module main (
  input  in_1,
  input  in_2
);

  wire undriven, undriven_2;

  // AND_Gate and_1 has open pins: in2=undriven_2, in3=undriven, out=open
  // OR_Gate or_1 has open pins: in1=undriven_2, in2=undriven, out=open
endmodule
